# Fritzing sketch arduinoISP (saved by Fritzing 1.0.1rc)
breadboards: 1
perfboards: 1

parts:
  IC1 = IC, DIP package, 14 pins [chip_label=QUARTZ]
  U1 = ZIFSOCKET-28-3 [package=dil28-3-zif_socket]
  R1 = Resistor [tolerance=±5% power=0.25W resistance=220 package=THT]
  R2 = Resistor [tolerance=±5% power=0.25W resistance=10k package=THT]
  LED1 = LED - 5mm [color="Red (633nm)" current=0.030A package="5 mm [THT]"]

nets:
  N1: IC1.pin7, U1.P$10, R1.Pin_1
  N2: IC1.pin8, U1.P$2
  N3: IC1.pin14, U1.P$28, R2.Pin_0
  N4: U1.P$1, R2.Pin_1
  N5: R1.Pin_0, LED1.cathode
